# Fritzing sketch FV-1 (saved by Fritzing 0.9.4)
breadboards: 2

parts:
  IC1 = Dual Op-Amp [package=dip08]
  R1 = Resistor [tolerance=±5% resistance=200k package=THT]
  C1 = Ceramic Capacitor [capacitance=100nF package="100 mil [THT, multilayer]"]
  R2 = Resistor [tolerance=±5% resistance=20k package=THT]
  R3 = Resistor [tolerance=±5% resistance=10k package=THT]
  C2 = Ceramic Capacitor [capacitance=100nF package="100 mil [THT, multilayer]"]
  R4 = Resistor [tolerance=±5% resistance=100k package=THT]
  R5 = Resistor [tolerance=±5% resistance=100k package=THT]
  C3 = Ceramic Capacitor [capacitance=100nF package="100 mil [THT, multilayer]"]
  R6 = Resistor [tolerance=±5% resistance=1M package=THT]
  R7 = Resistor [tolerance=±5% resistance=47k package=THT]
  R8 = Resistor [tolerance=±5% resistance=47k package=THT]
  C4 = Electrolytic Capacitor [capacitance=1µF package="100 mil [THT, electrolytic]"]
  C5 = Electrolytic Capacitor [capacitance=1µF package="100 mil [THT, electrolytic]"]
  C6 = Ceramic Capacitor [capacitance=100nF package="100 mil [THT, multilayer]"]
  U1 = mystery part, 18 pins [chip_label=FV-1]
  R9 = Resistor [tolerance=±5% resistance=1k package=THT]
  C7 = Ceramic Capacitor [capacitance=100nF package="100 mil [THT, multilayer]"]
  C8 = Ceramic Capacitor [capacitance=100nF package="100 mil [THT, multilayer]"]
  C9 = Ceramic Capacitor [capacitance=100nF package="100 mil [THT, multilayer]"]
  R10 = Resistor [tolerance=±5% resistance=1k package=THT]
  R11 = Resistor [tolerance=±5% resistance=1k package=THT]
  C10 = Ceramic Capacitor [capacitance=100nF package="100 mil [THT, multilayer]"]
  C11 = Ceramic Capacitor [capacitance=100nF package="100 mil [THT, multilayer]"]
  R12 = Resistor [tolerance=±5% resistance=10k package=THT]
  R13 = Resistor [tolerance=±5% resistance=10k package=THT]
  R14 = Rotary Potentiometer (Small) [maximum_resistance=100kΩ package=THT]
  C12 = Ceramic Capacitor [capacitance=100nF package="100 mil [THT, multilayer]"]
  R15 = Resistor [tolerance=±5% resistance=4.7k package=THT]

nets:
  N1: IC1.A_OUT, R1.Pin_0, C1.0, R2.Pin_1, C7.0
  N2: IC1.A_-IN, R1.Pin_1, C1.1, R5.Pin_0
  N3: IC1.A_+IN, IC1.B_+IN, R7.Pin_1, R8.Pin_0, C4.+
  N4: IC1.A_V-, R4.Pin_1, R6.Pin_1, R8.Pin_1, C4.-, C5.-, C6.1, U1.pin4, U1.pin7, U1.pin16, C8.0, C9.0, C11.1, R13.Pin_0, R14.leg1
  N5: IC1.B_-IN, R2.Pin_0, R3.Pin_1, R15.Pin_1
  N6: IC1.B_OUT, R3.Pin_0, C2.1
  N7: IC1.A_V+, R7.Pin_0, C5.+, C6.0
  N8: C2.0, R4.Pin_0
  N9: R5.Pin_1, C3.0
  N10: C3.1, R6.Pin_0
  N11: U1.pin1, U1.pin2, R9.Pin_1, C8.1
  N12: U1.pin3, C9.1
  N13: U1.pin5, U1.pin6, U1.pin13, U1.pin15, R12.Pin_0
  N14: U1.pin14, R12.Pin_1, R13.Pin_1
  N15: U1.pin17, R10.Pin_1
  N16: U1.pin18, R11.Pin_1
  N17: R9.Pin_0, C7.1
  N18: R10.Pin_0, R11.Pin_0, C10.1
  N19: C10.0, C11.0, R14.leg2
  N20: R14.wiper, C12.0
  N21: C12.1, R15.Pin_0

notes:
  OUT
  IN
  VCC/2
  VCC (9V)
  GND
  VCC/2
  FV-1 Module
  1 LIN 18 LOUT
  2 RIN 17 ROUT
  3 MID 16 POT2
  4 GND 15 POT1
  5 AVDD 14 POT0
  6 DVDD 13 DVDD
  7 T0 12 S2
  8 SCL 11 S1
  9 SDA 10 S0
  GND
  3.3V
