# Fritzing sketch FV-1_simple (saved by Fritzing 0.9.4)
breadboards: 1

parts:
  U1 = mystery part, 18 pins [chip_label=FV-1]
  R9 = Resistor [tolerance=±5% resistance=1k package=THT]
  C7 = Ceramic Capacitor [capacitance=100nF package="100 mil [THT, multilayer]"]
  C8 = Ceramic Capacitor [capacitance=100nF package="100 mil [THT, multilayer]"]
  C9 = Ceramic Capacitor [capacitance=100nF package="100 mil [THT, multilayer]"]
  R10 = Resistor [tolerance=±5% resistance=1k package=THT]
  R11 = Resistor [tolerance=±5% resistance=1k package=THT]
  C10 = Ceramic Capacitor [capacitance=100nF package="100 mil [THT, multilayer]"]
  C11 = Ceramic Capacitor [capacitance=100nF package="100 mil [THT, multilayer]"]
  R12 = Resistor [tolerance=±5% resistance=10k package=THT]
  R13 = Resistor [tolerance=±5% resistance=10k package=THT]
  R14 = Rotary Potentiometer (Small) [maximum_resistance=100kΩ package=THT]
  C12 = Ceramic Capacitor [capacitance=100nF package="100 mil [THT, multilayer]"]
  R15 = Resistor [tolerance=±5% resistance=4.7k package=THT]

nets:
  N1: U1.pin1, U1.pin2, R9.Pin_1, C8.1
  N2: U1.pin3, C9.1
  N3: U1.pin4, U1.pin7, U1.pin16, C8.0, C9.0, C11.1, R13.Pin_0, R14.leg1, R15.Pin_0
  N4: U1.pin5, U1.pin6, U1.pin13, U1.pin15, R12.Pin_0
  N5: U1.pin14, R12.Pin_1, R13.Pin_1
  N6: U1.pin17, R10.Pin_1
  N7: U1.pin18, R11.Pin_1
  N8: R9.Pin_0, C7.1
  N9: R10.Pin_0, R11.Pin_0, C10.1
  N10: C10.0, C11.0, R14.leg2
  N11: R14.wiper, C12.0
  N12: C12.1, R15.Pin_1

notes:
  FV-1 Module
  1 LIN 18 LOUT
  2 RIN 17 ROUT
  3 MID 16 POT2
  4 GND 15 POT1
  5 AVDD 14 POT0
  6 DVDD 13 DVDD
  7 T0 12 S2
  8 SCL 11 S1
  9 SDA 10 S0
  GND
  3.3V
  OUT
  IN
