# Fritzing sketch FV-1_interface_combination_test (saved by Fritzing 0.9.4)
breadboards: 1
perfboards: 1

parts:
  IC1 = Dual Op-Amp [package=dip08]
  C1 = Ceramic Capacitor [capacitance=100nF package="100 mil [THT, multilayer]"]
  C2 = Ceramic Capacitor [capacitance=100nF package="100 mil [THT, multilayer]"]
  R1 = Resistor [tolerance=±5% resistance=100k package=THT]
  C3 = Ceramic Capacitor [capacitance=100nF package="100 mil [THT, multilayer]"]
  R2 = Resistor [tolerance=±5% resistance=330k package=THT]
  R3 = Rotary Potentiometer (Small) [maximum_resistance=100kΩ package=THT]
  C5 = Film/Foil Capacitor [capacitance=100nF voltage=35V package="5mm [THT, pp]"]
  R4 = Rotary Potentiometer (Small) [maximum_resistance=100kΩ package=THT]
  C6 = Film/Foil Capacitor [capacitance=100nF voltage=35V package="5mm [THT, pp]"]
  R5 = Resistor [tolerance=±5% resistance=330k package=THT]
  C8 = Electrolytic Capacitor [capacitance=1µF package="100 mil [THT, electrolytic]"]
  C9 = Electrolytic Capacitor [capacitance=1µF package="100 mil [THT, electrolytic]"]
  R7 = Resistor [tolerance=±5% resistance=1k package=THT]
  R8 = Resistor [tolerance=±5% resistance=100k package=THT]
  J1 = female pin header, 2 pins [form="♀ (female)"]
  J2 = female pin header, 2 pins [form="♀ (female)"]
  J3 = female pin header, 2 pins [form="♀ (female)"]
  Power_plug1 = Power plug
  R9 = Rotary Potentiometer (Small) [maximum_resistance=100kΩ package=THT]  # not connected
  R10 = Rotary Potentiometer (Small) [maximum_resistance=100kΩ package=THT]  # not connected
  R11 = Rotary Potentiometer (Small) [maximum_resistance=100kΩ package=THT]  # not connected
  J4 = female pin header, 2 pins [form="♀ (female)"]  # not connected
  U1 = AUDIO-JACK2 [package=audio-jack]

nets:
  N1: IC1.A_OUT, R1.Pin_0, C3.0, R4.leg1, J1.pin1
  N2: IC1.A_-IN, R1.Pin_1, C3.1, R2.Pin_1
  N3: IC1.A_+IN, IC1.B_+IN, C1.0, C2.1, R3.leg1, C8.-, C9.+, J1.pin2, J2.pin2, U1.SLEEVE
  N4: IC1.A_V-, C1.1, C9.-
  N5: IC1.B_-IN, R5.Pin_0, R8.Pin_1
  N6: IC1.B_OUT, R5.Pin_1, R7.Pin_0
  N7: IC1.A_V+, C2.0, C8.+
  N8: R2.Pin_0, C5.+
  N9: R3.wiper, C5.-
  N10: R3.leg2, U1.TIP
  N11: R4.wiper, R8.Pin_0
  N12: R4.leg2, C6.+
  N13: C6.-, J2.pin1
  N14: J3.pin1, Power_plug1.VCC
  N15: J3.pin2, Power_plug1.GND

notes:
  IN
  50k/A
  OUT
  GND
  +12V
  -12V
  GND
  50k/B
  3.3V
  FV-1 Test Board
  Left Out
